# Fritzing sketch DistanceDetectorModel (saved by Fritzing 0.9.3b)
breadboards: 1

parts:
  LCD1 = LCD screen
  Part1 = Arduino Uno (Rev3)
  hc-sr1 = hc-sr04
  R1 = Resistor [tolerance=±5% resistance=220 package=THT]
  R2 = Resistor [tolerance=±5% resistance=220 package=THT]

nets:
  GND: LCD1.VSS, LCD1.R/W, Part1.GND, hc-sr1.GND, R1.Pin_1
  VDD: LCD1.VDD, Part1.5V, hc-sr1.VCC, R2.Pin_1
  N1: LCD1.V0, R1.Pin_0
  N2: LCD1.RS, Part1.D12/MISO
  N3: LCD1.E, Part1.D11_PWM/MOSI
  N4: LCD1.DB4, Part1.D5_PWM
  N5: LCD1.DB5, Part1.D4
  N6: LCD1.DB6, Part1.D3_PWM
  N7: LCD1.DB7, Part1.D2
  N8: LCD1.LED+, R2.Pin_0
  N9: Part1.D9_PWM, hc-sr1.Echo
  N10: Part1.D10_PWM/SS, hc-sr1.Trig
